# Fritzing sketch ringer4 (saved by Fritzing 0.9.3b)
circuit board: 8.53488cm x 5.63626cm
breadboards: 1

parts:
  Q1 = Basic FET P-Channel [package="TO220 [THT]"]
  Bell = Screw terminal - 2 pins [package=THT]
  Magneto = Screw terminal - 2 pins [package=THT]
  Raspberry_Pi_1 = Raspberry Pi 3 [part_number=RPI-3-V1.2]
  IC2 = NJM2670 [package="NJM2670D2 (DIP22)"]
  R2 = Resistor [tolerance=±5% resistance=180 package=THT]
  D1 = Schottky Diode [part_number=1N5817 package="300 mil [THT]"]
  R4 = Resistor [tolerance=±5% resistance=2.2k package=THT]
  C1 = Ceramic Capacitor [capacitance=1nF package="100 mil [THT, multilayer]"]
  C4 = Electrolytic Capacitor [capacitance=100µF voltage=50V package="200 mil [THT, electrolytic]"]
  R5 = Resistor [tolerance=±5% resistance=47k package=THT]
  IC1 = MC34063AP [chip_label=MC34063AP part_number=MC34063AP package="DIP (Dual Inline) [THT]"]
  C2 = Electrolytic Capacitor [capacitance=100µF package="100 mil [THT, electrolytic]"]
  C3 = Ceramic Capacitor [capacitance=100nF package="100 mil [THT, multilayer]"]
  C5 = Electrolytic Capacitor [capacitance=3.3µF voltage=50V package="100 mil [THT, electrolytic]"]
  L1 = RCP1317 [package="13 cm [THT]"]
  R3 = 0.22 Ω Resistor [package=THT]
  U1 = RT314F03 [part_number=RT314F03 package=OJ]
  Q2 = NPN-Transistor [package="TO92 [THT]"]
  Q3 = NPN-Transistor [package="TO92 [THT]"]
  D2 = Rectifier Diode [part_number=1N4001 package="300 mil [THT]"]
  D3 = Rectifier Diode [part_number=1N4001 package="300 mil [THT]"]
  R6 = Resistor [tolerance=±5% resistance=1k package="0603 [SMD]"]
  R7 = Resistor [tolerance=±5% resistance=1k package="0603 [SMD]"]
  Hook_SW = Screw terminal - 2 pins [package=THT]
  PWR = smd LED [color="Yellow (595nm)" package="0603 [SMD]"]
  R1 = Resistor [tolerance=±5% resistance=140 package="0603 [SMD]"]
  R8 = Resistor [tolerance=±5% resistance=3.5k package="2010 [SMD]"]
  R9 = Resistor [tolerance=±5% resistance=3.5k package="2010 [SMD]"]
  IC3 = PDIP06 [part_number=H11AA1SM chip_label=H11AA1SM package=PDIP]

nets:
  N1: Q1.gate, Raspberry_Pi_1.GPIO4
  VCC: Q1.drain, IC2.ENABLE_A, IC2.VCC, IC1.VCC, C2.+, C3.0, R3.Pin_0, PWR.anode
  N2: Q1.source, Raspberry_Pi_1.5V
  N3: Bell.pin1, Magneto.pin1, IC2.OUT_A1, R9.Pin_1
  N4: Bell.pin2, C5.-, U1.12#5, U1.11, U1.14
  N5: Magneto.pin2, U1.12#4, R8.Pin_1
  3V3: Raspberry_Pi_1.3v3, Raspberry_Pi_1.3V3, U1.A3, D2.cathode, D3.cathode
  GND: Raspberry_Pi_1.GND, IC2.SENSE_A, IC2.GND, IC2.ENABLE_B, R4.Pin_1, C1.0, C4.-, IC1.Switch_Emitter, IC1.GND, C2.-, C3.1, Q2.E, Q3.E, Hook_SW.pin1, R1.Pin_0, IC3.4
  N6: Raspberry_Pi_1.GPIO27, IC2.IN_A
  N7: Raspberry_Pi_1.GPIO22, IC2.IN_A2
  N8: Raspberry_Pi_1.GPIO5, R6.Pin_0
  N9: Raspberry_Pi_1.GPIO6, R7.Pin_1
  N10: Raspberry_Pi_1.GPIO19, Hook_SW.pin2
  N11: Raspberry_Pi_1.GPIO26, IC3.5
  N12: IC2.OUT_A2, C5.+
  N13: IC2.VS_A, D1.anode, C4.+, R5.Pin_1
  N14: R2.Pin_0, IC1.Drive_Collector
  N15: R2.Pin_1, IC1.Ipk, L1.pin_0, R3.Pin_1
  N16: D1.cathode, IC1.Switch_Collector, L1.pin_1
  N17: R4.Pin_0, R5.Pin_0, IC1.Comparator_Inverting_Input
  N18: C1.1, IC1.Timing_Capacitor
  N19: U1.A1, Q3.C, D3.anode
  N20: U1.A2, Q2.C, D2.anode
  N21: Q2.B, R6.Pin_1
  N22: Q3.B, R7.Pin_0
  N23: PWR.cathode, R1.Pin_1
  N24: R8.Pin_0, IC3.2
  N25: R9.Pin_0, IC3.1

notes:
  cranky rev. A
  MAG EN
  RING EN
  +3v
  (output)

custom parts:
  RCP1317: Inductor
  0.22 Ω Resistor: BPR58 0.22 Ω 5W Resistor
  RT314F03: Two-coil bistable SPDT Relay
